# Fritzing sketch NeoPixel Corner (saved by Fritzing 0.9.3b)
circuit board: 1.01cm x 1.01cm
breadboards: 1

parts:
  5050 = ws2812b [package="smd 2812b"]
  J1 = Generic single row SMD pads - 4 pins [package=SMD]
  J2 = Generic single row SMD pads - 4 pins [package=SMD]

nets:
  N1: 5050.VDD, J1.pin2, J2.pin2
  N2: 5050.DOUT, J2.pin3
  N3: 5050.VSS, J1.pin1, J1.pin4, J2.pin1, J2.pin4
  N4: 5050.DIN, J1.pin3

custom parts:
  Generic single row SMD pads - 4 pins: Generic single row SMD female pads
